// Logisim project 4BIT_CPU.circ as structural Verilog: 5 circuits, main circuit main
module main (
  input  SUB,
  input  CIN,
  input  [2:0] select_op,
  input  A,
  input  B,
  input  in_6,
  output RESULT,
  output COUT,
  output out_9
);

  wire and_1_out, nor_1_out, or_1_out, xor_1_out, xor_2_out;

  xor xor_1 (xor_1_out, B, SUB);
  and and_1 (and_1_out, A, B);
  or or_1 (or_1_out, A, B);
  xor xor_2 (xor_2_out, A, B);
  nor nor_1 (nor_1_out, A, B);
  Adder #(.width(1)) adder_1 (.a(A), .b(xor_1_out), .out(out_9), .cin(CIN), .cout(COUT));
  Multiplexer #(.select(3)) multiplexer_1 (
    .in0(and_1_out), .in1(or_1_out), .in2(xor_2_out), .in3(nor_1_out), .in4(out_9), .in5(in_6), .out(RESULT),
    .sel(select_op));  // open: in6, in7, en
endmodule

module _4bit_ALU_CPU (
  input  SUB,
  input  [2:0] OP,
  input  [3:0] A,
  input  [3:0] B,
  output [3:0] OUTPUT
);

  wire main_1_cout, main_2_cout, main_3_cout, main_4_out_9;

  main main_1 (
    .A(A[0]), .B(B[0]), .RESULT(OUTPUT[0]), .SUB(SUB), .CIN(SUB), .select_op(OP), .COUT(main_1_cout),
    .in_6(main_4_out_9));  // open: out_9
  main main_2 (
    .A(A[1]), .B(B[1]), .RESULT(OUTPUT[1]), .SUB(SUB), .CIN(main_1_cout), .select_op(OP), .COUT(main_2_cout),
    .in_6(1'b0));  // open: out_9
  main main_3 (
    .A(A[2]), .B(B[2]), .RESULT(OUTPUT[2]), .SUB(SUB), .CIN(main_2_cout), .select_op(OP), .COUT(main_3_cout),
    .in_6(1'b0));  // open: out_9
  main main_4 (
    .A(A[3]), .B(B[3]), .RESULT(OUTPUT[3]), .SUB(SUB), .CIN(main_3_cout), .select_op(OP), .in_6(1'b0),
    .out_9(main_4_out_9));  // open: COUT

  // Notes on the sheet:
  //   function selector
  //   RESULT
  //   function selector:
  //   000= AND
  //   001= OR
  //   010= NOT
  //   011=XOR
  //   100=ADD
  //   101=SUB
endmodule

module ALU_2 (
  input  [3:0] A,
  input  [3:0] B,
  input  [1:0] OP,
  output [3:0] out_4
);

  wire [3:0] adder_1_out, and_1_out, or_1_out, xor_1_out;

  Adder #(.width(4)) adder_1 (.a(A), .b(B), .out(adder_1_out), .cin(1'b0));  // open: cout
  assign and_1_out = A & B;  // AND_Gate and_1, 4 bits wide
  assign or_1_out = A | B;  // OR_Gate or_1, 4 bits wide
  assign xor_1_out = A ^ B;  // XOR_Gate xor_1, 4 bits wide
  Multiplexer #(.select(2), .width(4), .disabled(0), .enable("false")) multiplexer_1 (
    .in0(adder_1_out), .in1(and_1_out), .in2(or_1_out), .in3(xor_1_out), .out(out_4), .sel(OP));
endmodule

module REGFILE (
  input  [3:0] INP,
  input  C,
  input  [2:0] RD,
  input  [2:0] RA,
  input  [2:0] RB,
  output [3:0] A,
  output [3:0] B
);

  wire demultiplexer_1_out0, demultiplexer_1_out1, demultiplexer_1_out2, demultiplexer_1_out3,
       demultiplexer_1_out4, demultiplexer_1_out5, demultiplexer_1_out6, demultiplexer_1_out7;
  wire [3:0] R0_q, R1_q, R2_q, R3_q, R4_q, R5_q, R6_q, R7_q;

  Demultiplexer #(.select(3), .enable("false")) demultiplexer_1 (
    .out0(demultiplexer_1_out0), .out1(demultiplexer_1_out1), .out2(demultiplexer_1_out2),
    .out3(demultiplexer_1_out3), .out4(demultiplexer_1_out4), .out5(demultiplexer_1_out5),
    .out6(demultiplexer_1_out6), .out7(demultiplexer_1_out7), .in(1'b1), .sel(RD));
  Register #(.width(4)) R0 (.D(INP), .en(demultiplexer_1_out0), .Q(R0_q), .clk(C));  // open: clr
  Register #(.width(4)) R1 (.D(INP), .en(demultiplexer_1_out1), .Q(R1_q), .clk(C));  // open: clr
  Register #(.width(4)) R2 (.D(INP), .en(demultiplexer_1_out2), .Q(R2_q), .clk(C));  // open: clr
  Register #(.width(4)) R3 (.D(INP), .en(demultiplexer_1_out3), .Q(R3_q), .clk(C));  // open: clr
  Register #(.width(4)) R4 (.D(INP), .en(demultiplexer_1_out4), .Q(R4_q), .clk(C));  // open: clr
  Register #(.width(4)) R5 (.D(INP), .en(demultiplexer_1_out5), .Q(R5_q), .clk(C));  // open: clr
  Register #(.width(4)) R6 (.D(INP), .en(demultiplexer_1_out6), .Q(R6_q), .clk(C));  // open: clr
  Register #(.width(4)) R7 (.D(INP), .en(demultiplexer_1_out7), .Q(R7_q), .clk(C));  // open: clr
  Multiplexer #(.select(3), .width(4), .enable("false")) multiplexer_1 (
    .in0(R0_q), .in1(R1_q), .in2(R2_q), .in3(R3_q), .in4(R4_q), .in5(R5_q), .in6(R6_q), .in7(R7_q), .out(A),
    .sel(RA));
  Multiplexer #(.select(3), .width(4), .enable("false")) multiplexer_2 (
    .in0(R0_q), .in1(R1_q), .in2(R2_q), .in3(R3_q), .in4(R4_q), .in5(R5_q), .in6(R6_q), .in7(R7_q), .out(B),
    .sel(RB));
endmodule

module CPU (
);

  wire CLK, DATA, MOV;
  wire [1:0] OP;
  wire [2:0] RD;
  wire [2:1] RA;
  wire [3:0] alu_2_1_out_4, controlled_buffer_1_out, counter_1_q, counter_1_q_2, NUM, regfile_1_a,
       regfile_1_b;
  wire [15:0] rom_1_data;
  wire [15:9] register_1_q;

  assign controlled_buffer_1_out = MOV ? NUM : 4'bz;  // Controlled_Buffer controlled_buffer_1
  Clock clock_1 (.out(CLK));
  Hex_Digit_Display hex_digit_display_1 (.value(counter_1_q_2));  // open: dp
  Hex_Digit_Display hex_digit_display_2 (.value(counter_1_q));  // open: dp
  Counter counter_1 (
    .load(1'b0), .count(1'b1), .Q({counter_1_q_2, counter_1_q}), .clk(CLK), .clr(1'b0));  // open: D, carry
  REGFILE regfile_1 (
    .INP(controlled_buffer_1_out), .C(CLK), .RD(RD), .A(regfile_1_a), .B(regfile_1_b), .RA({RA, NUM[3]}),
    .RB(NUM[2:0]));
  assign controlled_buffer_1_out = DATA ? alu_2_1_out_4 : 4'bz;  // Controlled_Buffer controlled_buffer_2
  ROM #(.dataWidth(16)) rom_1 (.addr({counter_1_q_2, counter_1_q}), .data(rom_1_data));  // open: sel
  Register #(.width(16)) register_1 (
    .D(rom_1_data), .en(1'b1), .Q({register_1_q[15:14], OP, register_1_q[11:9], RA, NUM, RD}), .clk(CLK),
    .clr(1'b0));
  ALU_2 alu_2_1 (.A(regfile_1_a), .B(regfile_1_b), .out_4(alu_2_1_out_4), .OP(OP));
  and and_1 (MOV, register_1_q[14], register_1_q[15]);
  and and_2 (DATA, ~register_1_q[14], ~register_1_q[15]);  // AND_Gate
  // Probe on nothing

  // Other names for the same wires on the sheet: RB[2:0] = NUM[2:0]; RA[0] = NUM[3]

  // Notes on the sheet:
  //   contents of rom_1 (hex, n*v repeats v):
  //   c024 c028 117 3116
endmodule
